// Logisim project project2.circ as structural Verilog: 1 circuit, main circuit main
module main (
  output [7:0] out_1,
  output [1:0] out_2,
  output [7:0] out_3,
  output [1:0] ReadReg1,
  output [7:0] RegData1,
  output [7:0] RegData2,
  output [1:0] ReadReg2,
  output [7:0] ReadPort,
  output [7:0] out_9
);

  wire and_1_out, and_2_out, and_3_out, and_4_out, CIock_out, clock_1_out, decoder_1_out0, decoder_1_out1,
       decoder_1_out2, decoder_1_out3;
  wire [3:0] multiplexer_1_out, multiplexer_1_out_2;
  wire [7:0] adder_1_out, PC_q, X0_q, X1_q, X2_q, X3_q;

  Clock clock_1 (.out(clock_1_out));
  Adder adder_1 (.a(PC_q), .b(8'h1), .out(adder_1_out));  // open: cin, cout
  RAM InstructionMemory (.addr(PC_q), .we(1'b0), .oe(1'b1), .clk(CIock_out), .dout(out_1));  // open: din
  Clock #(.highDuration(2), .lowDuration(2)) CIock (.out(CIock_out));
  RAM #(.addrWidth(4)) DataMemory (
    .addr(out_1[5:2]), .we(1'b0), .oe(1'b1), .clk(clock_1_out), .dout(ReadPort));  // open: din
  Register PC (.D(adder_1_out), .en(1'b1), .clk(CIock_out), .Q(PC_q));  // open: clr
  Multiplexer #(.select(2), .width(8)) multiplexer_1 (
    .in0(ReadPort), .in1(out_3), .in2(out_9), .out({multiplexer_1_out_2, multiplexer_1_out}), .sel(out_1[7:6]));  // open: in3
  Decoder #(.select(2)) decoder_1 (
    .out0(decoder_1_out0), .out1(decoder_1_out1), .out2(decoder_1_out2), .out3(decoder_1_out3),
    .sel(out_1[1:0]));  // open: en
  Adder adder_2 (.a(RegData1), .b(RegData2), .out(out_3));  // open: cin, cout
  Subtractor subtractor_1 (.a(RegData1), .b(RegData2), .out(out_9));  // open: bin, bout
  and and_1 (and_1_out, 1'b1, decoder_1_out0);
  and and_2 (and_2_out, 1'b1, decoder_1_out1);
  and and_3 (and_3_out, 1'b1, decoder_1_out2);
  and and_4 (and_4_out, 1'b1, decoder_1_out3);
  Hex_Digit_Display hex_digit_display_1 (.value(multiplexer_1_out_2));  // open: dp
  Hex_Digit_Display hex_digit_display_2 (.value(multiplexer_1_out));  // open: dp
  Register X0 (.D({multiplexer_1_out_2, multiplexer_1_out}), .en(and_1_out), .clk(CIock_out), .Q(X0_q));  // open: clr
  Register X1 (.D({multiplexer_1_out_2, multiplexer_1_out}), .en(and_2_out), .clk(CIock_out), .Q(X1_q));  // open: clr
  Register X2 (.D({multiplexer_1_out_2, multiplexer_1_out}), .en(and_3_out), .clk(CIock_out), .Q(X2_q));  // open: clr
  Register X3 (.D({multiplexer_1_out_2, multiplexer_1_out}), .en(and_4_out), .clk(CIock_out), .Q(X3_q));  // open: clr
  Multiplexer #(.select(2), .width(8)) multiplexer_2 (
    .in0(X0_q), .in1(X1_q), .in2(X2_q), .in3(X3_q), .out(RegData1), .sel(out_1[5:4]));
  Multiplexer #(.select(2), .width(8)) multiplexer_3 (
    .in0(X0_q), .in1(X1_q), .in2(X2_q), .in3(X3_q), .out(RegData2), .sel(out_1[3:2]));

  assign out_2 = out_1[7:6];
  assign ReadReg1 = out_1[5:4];
  assign ReadReg2 = out_1[3:2];

  // Notes on the sheet:
  //   Belal Eltemsah & Joanne Wang
  //   I pledge my honor that I have abided by the Stevens Honor System
  //   Instruction Memory
  //   Data Memory
  //   The Spectra Hyper Ultra
  //   Dynamic Operating Neural Grid
  //   (The S.H.U.D.O.N.G)
  //   RegWrite
  //   ALU
  //   ADD
  //   SUB
endmodule
